// Logisim project LogicAlarm.circ as structural Verilog: 3 circuits, main circuit main
module main (
  input  [3:0] in_1,
  input  [3:0] in_2,
  input  [3:0] in_3,
  input  [3:0] in_4,
  input  [3:0] in_5,
  input  [3:0] in_6
);

  wire [2:0] sixsegdriver_1_bottom1, sixsegdriver_1_bottom2, sixsegdriver_1_bottom3, sixsegdriver_1_bottom4,
       sixsegdriver_1_bottom5, sixsegdriver_1_bottom6;
  wire [3:0] sixsegdriver_1_top1, sixsegdriver_1_top2, sixsegdriver_1_top3, sixsegdriver_1_top4,
       sixsegdriver_1_top5, sixsegdriver_1_top6;

  sixSegDriver sixsegdriver_1 (
    .Seg1(in_1), .Seg2(in_2), .Seg3(in_3), .Seg4(in_4), .Seg5(in_5), .Seg6(in_6), .Top1(sixsegdriver_1_top1),
    .Bottom1(sixsegdriver_1_bottom1), .Top2(sixsegdriver_1_top2), .Bottom2(sixsegdriver_1_bottom2),
    .Top3(sixsegdriver_1_top3), .Bottom3(sixsegdriver_1_bottom3), .Top4(sixsegdriver_1_top4),
    .Bottom4(sixsegdriver_1_bottom4), .Top5(sixsegdriver_1_top5), .Bottom5(sixsegdriver_1_bottom5),
    .Top6(sixsegdriver_1_top6), .Bottom6(sixsegdriver_1_bottom6));
  _7_Segment_Display seg6 (
    .g(sixsegdriver_1_top6[3]), .f(sixsegdriver_1_top6[2]), .a(sixsegdriver_1_top6[1]),
    .b(sixsegdriver_1_top6[0]), .e(sixsegdriver_1_bottom6[0]), .d(sixsegdriver_1_bottom6[1]),
    .c(sixsegdriver_1_bottom6[2]));  // open: dp
  _7_Segment_Display seg5 (
    .g(sixsegdriver_1_top5[3]), .f(sixsegdriver_1_top5[2]), .a(sixsegdriver_1_top5[1]),
    .b(sixsegdriver_1_top5[0]), .e(sixsegdriver_1_bottom5[0]), .d(sixsegdriver_1_bottom5[1]),
    .c(sixsegdriver_1_bottom5[2]));  // open: dp
  _7_Segment_Display seg4 (
    .g(sixsegdriver_1_top4[3]), .f(sixsegdriver_1_top4[2]), .a(sixsegdriver_1_top4[1]),
    .b(sixsegdriver_1_top4[0]), .e(sixsegdriver_1_bottom4[0]), .d(sixsegdriver_1_bottom4[1]),
    .c(sixsegdriver_1_bottom4[2]));  // open: dp
  _7_Segment_Display seg3 (
    .g(sixsegdriver_1_top3[3]), .f(sixsegdriver_1_top3[2]), .a(sixsegdriver_1_top3[1]),
    .b(sixsegdriver_1_top3[0]), .e(sixsegdriver_1_bottom3[0]), .d(sixsegdriver_1_bottom3[1]),
    .c(sixsegdriver_1_bottom3[2]));  // open: dp
  _7_Segment_Display seg2 (
    .g(sixsegdriver_1_top2[3]), .f(sixsegdriver_1_top2[2]), .a(sixsegdriver_1_top2[1]),
    .b(sixsegdriver_1_top2[0]), .e(sixsegdriver_1_bottom2[0]), .d(sixsegdriver_1_bottom2[1]),
    .c(sixsegdriver_1_bottom2[2]));  // open: dp
  _7_Segment_Display seg1 (
    .g(sixsegdriver_1_top1[3]), .f(sixsegdriver_1_top1[2]), .a(sixsegdriver_1_top1[1]),
    .b(sixsegdriver_1_top1[0]), .e(sixsegdriver_1_bottom1[0]), .d(sixsegdriver_1_bottom1[1]),
    .c(sixsegdriver_1_bottom1[2]));  // open: dp
endmodule

module segDriver (
  input  B3,
  input  B2,
  input  B1,
  input  B0,
  output [3:0] Top,
  output [2:0] Bottom
);

  wire and_1_out, and_2_out, and_3_out, and_4_out, and_5_out, and_6_out, and_7_out, and_8_out, and_9_out,
       and_10_out, and_11_out, and_12_out, and_13_out, and_14_out, and_15_out, and_16_out, and_17_out,
       and_18_out, and_19_out, and_20_out, and_21_out, and_22_out, and_23_out, and_24_out, and_25_out,
       and_26_out, and_27_out, and_28_out, not_1_out, not_2_out, not_3_out, not_4_out, not_5_out, not_6_out,
       not_7_out, not_8_out, not_9_out, not_10_out, not_11_out, not_12_out, not_13_out, not_14_out,
       not_15_out, not_16_out, not_17_out, not_18_out, not_19_out, not_20_out, not_21_out, not_22_out,
       not_23_out, not_24_out, not_25_out, not_26_out, not_27_out, not_28_out, not_29_out, not_30_out,
       not_31_out, not_32_out, not_33_out, not_34_out, not_35_out, not_36_out, not_37_out, not_38_out,
       not_39_out, not_40_out, not_41_out, not_42_out, not_43_out, not_44_out, or_4_out;
  wire [2:0] undriven_2;
  wire [3:0] undriven;

  not not_1 (not_1_out, B1);
  not not_2 (not_2_out, B2);
  not not_3 (not_3_out, B3);
  not not_4 (not_4_out, B1);
  not not_5 (not_5_out, B0);
  not not_6 (not_6_out, B3);
  not not_7 (not_7_out, B2);
  not not_8 (not_8_out, B1);
  not not_9 (not_9_out, B3);
  not not_10 (not_10_out, B3);
  not not_11 (not_11_out, B1);
  not not_12 (not_12_out, B0);
  not not_13 (not_13_out, B3);
  not not_14 (not_14_out, B2);
  not not_15 (not_15_out, B0);
  not not_16 (not_16_out, B3);
  not not_17 (not_17_out, B2);
  not not_18 (not_18_out, B0);
  not not_19 (not_19_out, B2);
  not not_20 (not_20_out, B1);
  not not_21 (not_21_out, B0);
  not not_22 (not_22_out, B1);
  not not_23 (not_23_out, B2);
  not not_24 (not_24_out, B0);
  not not_25 (not_25_out, B0);
  not not_26 (not_26_out, B1);
  not not_27 (not_27_out, B3);
  not not_28 (not_28_out, B3);
  not not_29 (not_29_out, B2);
  not not_30 (not_30_out, B3);
  not not_31 (not_31_out, B2);
  not not_32 (not_32_out, B1);
  not not_33 (not_33_out, B1);
  not not_34 (not_34_out, B0);
  not not_35 (not_35_out, B3);
  not not_36 (not_36_out, B3);
  not not_37 (not_37_out, B2);
  not not_38 (not_38_out, B1);
  and and_1 (and_1_out, B3, B2, not_1_out, B0);
  and and_2 (and_2_out, B3, not_2_out, B1, B0);
  and and_3 (and_3_out, not_3_out, B2, not_4_out, not_5_out);
  and and_4 (and_4_out, not_6_out, not_7_out, not_8_out, B0);
  not not_39 (not_39_out, B2);
  and and_5 (and_5_out, not_39_out, not_40_out);
  not not_40 (not_40_out, B0);
  and and_6 (and_6_out, B0, B3, not_41_out);
  not not_41 (not_41_out, B1);
  and and_7 (and_7_out, not_9_out, B2, B1, B0);
  and and_8 (and_8_out, not_10_out, B2, not_11_out, not_12_out);
  not not_42 (not_42_out, B3);
  and and_9 (and_9_out, not_42_out, not_43_out, B0);
  not not_43 (not_43_out, B2);
  and and_10 (and_10_out, B3, B2, not_44_out);
  not not_44 (not_44_out, B0);
  and and_11 (and_11_out, B3, B2, B1, B0);
  and and_12 (and_12_out, not_13_out, not_14_out, B1, not_15_out);
  and and_13 (and_13_out, not_16_out, not_17_out, not_18_out);
  and and_14 (and_14_out, not_19_out, B1, B0);
  and and_15 (and_15_out, B2, not_20_out, B0);
  and and_16 (and_16_out, B2, B1, not_21_out);
  and and_17 (and_17_out, B3, not_22_out);
  and and_18 (and_18_out, not_23_out, not_24_out);
  and and_19 (and_19_out, B1, not_25_out);
  and and_20 (and_20_out, B3, B1);
  and and_21 (and_21_out, B3, B2);
  and and_22 (and_22_out, B3, B2, not_26_out, B0);
  and and_23 (and_23_out, not_27_out, B2, B1, B0);
  and and_24 (and_24_out, not_28_out, not_29_out, B1);
  and and_25 (and_25_out, not_30_out, not_31_out, not_32_out, B0);
  and and_26 (and_26_out, B3, B2, not_33_out, not_34_out);
  and and_27 (and_27_out, not_35_out, B2, B1, B0);
  and and_28 (and_28_out, not_36_out, not_37_out, not_38_out);
  or or_1 (Top[0], and_5_out, and_6_out, and_7_out, and_8_out, and_9_out);
  nor nor_1 (Bottom[2], and_10_out, and_11_out, and_12_out);
  or or_2 (Bottom[1], and_13_out, and_14_out, and_15_out, and_16_out, and_17_out);
  or or_3 (Bottom[0], and_18_out, and_19_out, and_20_out, and_21_out);
  nor nor_2 (Top[2], and_22_out, and_23_out, and_24_out, and_25_out);
  nor nor_3 (Top[3], and_26_out, and_27_out, and_28_out);
  or or_4 (or_4_out, and_1_out, and_2_out, and_3_out, and_4_out);
  not not_45 (Top[1], or_4_out);
  _7_Segment_Display u_7_segment_display_1 (
    .g(undriven[3]), .f(undriven[2]), .a(undriven[1]), .b(undriven[0]), .e(undriven_2[0]), .d(undriven_2[1]),
    .c(undriven_2[2]));  // open: dp
endmodule

module sixSegDriver (
  input  [3:0] Seg1,
  input  [3:0] Seg2,
  input  [3:0] Seg3,
  input  [3:0] Seg4,
  input  [3:0] Seg5,
  input  [3:0] Seg6,
  output [3:0] Top1,
  output [2:0] Bottom1,
  output [3:0] Top2,
  output [2:0] Bottom2,
  output [3:0] Top3,
  output [2:0] Bottom3,
  output [3:0] Top4,
  output [2:0] Bottom4,
  output [3:0] Top5,
  output [2:0] Bottom5,
  output [3:0] Top6,
  output [2:0] Bottom6
);

  segDriver segdriver_1 (.B3(Seg1[3]), .B2(Seg1[2]), .B1(Seg1[1]), .B0(Seg1[0]), .Top(Top1), .Bottom(Bottom1));
  segDriver segdriver_2 (.B3(Seg2[3]), .B2(Seg2[2]), .B1(Seg2[1]), .B0(Seg2[0]), .Top(Top2), .Bottom(Bottom2));
  segDriver segdriver_3 (.B3(Seg3[3]), .B2(Seg3[2]), .B1(Seg3[1]), .B0(Seg3[0]), .Top(Top3), .Bottom(Bottom3));
  segDriver segdriver_4 (.B3(Seg4[3]), .B2(Seg4[2]), .B1(Seg4[1]), .B0(Seg4[0]), .Top(Top4), .Bottom(Bottom4));
  segDriver segdriver_5 (.B3(Seg5[3]), .B2(Seg5[2]), .B1(Seg5[1]), .B0(Seg5[0]), .Top(Top5), .Bottom(Bottom5));
  segDriver segdriver_6 (.B3(Seg6[3]), .B2(Seg6[2]), .B1(Seg6[1]), .B0(Seg6[0]), .Top(Top6), .Bottom(Bottom6));
endmodule
